// Logisim project floating-point-adder.circ as structural Verilog: 4 circuits, main circuit ExponentDiff
module main (
  input  [15:0] A,
  input  [15:0] B,
  output Output_Sign,
  output [10:0] Output__Fraction,
  output [12:0] Un_F,
  output [12:0] F1_With_sign,
  output [12:0] F2__With_sign,
  output [3:0] out_8,
  output [12:0] out_9,
  output out_10,
  output [3:0] Output_Exponent,
  output [3:0] out_12
);

  wire undriven;
  wire [3:0] exponentdiff_1_max_a_b, exponentdiff_2_abs_a_b, exponentdiff_3_abs_a_b, subtractor_2_out;
  wire [11:0] shifter_1_out, shifter_2_out;
  wire [12:0] adder_1_out;

  ExponentDiff exponentdiff_1 (.A(A[14:11]), .B(B[14:11]), .Max_A_B(exponentdiff_1_max_a_b));  // open: abs_A_B
  ExponentDiff exponentdiff_2 (
    .A(exponentdiff_1_max_a_b), .B(A[14:11]), .abs_A_B(exponentdiff_2_abs_a_b));  // open: Max_A_B
  Shifter #(.width(12), .shift("lr")) shifter_1 (
    .in({1'b1, A[10:0]}), .\dist (exponentdiff_2_abs_a_b), .out(shifter_1_out));
  ExponentDiff exponentdiff_3 (
    .A(exponentdiff_1_max_a_b), .B(B[14:11]), .abs_A_B(exponentdiff_3_abs_a_b));  // open: Max_A_B
  fraction_sign_set fraction_sign_set_1 (.F(shifter_1_out), .S(A[15]), .F_prime(F1_With_sign));
  Shifter #(.width(12), .shift("lr")) shifter_2 (
    .in({1'b1, B[10:0]}), .\dist (exponentdiff_3_abs_a_b), .out(shifter_2_out));
  fraction_sign_set fraction_sign_set_2 (.F(shifter_2_out), .S(B[15]), .F_prime(F2__With_sign));
  Adder #(.width(13)) adder_1 (.a(F2__With_sign), .b(F1_With_sign), .out(adder_1_out), .cin(1'b0), .cout(out_10));
  twos_complement_if_negative twos_complement_if_negative_1 (
    .in_1({out_10, adder_1_out}), .Output(Un_F));  // open: Sign
  BitFinder #(.width(13), .\type ("high1")) bitfinder_1 (.in(Un_F), .index(out_8));  // open: found
  Subtractor #(.width(4)) subtractor_1 (.a(4'b1100), .b(out_8), .out(out_12), .bin(1'b0));  // open: bout
  Shifter #(.width(13)) shifter_3 (.in(Un_F), .\dist (out_12), .out(out_9));
  Subtractor #(.width(4)) subtractor_2 (
    .a(exponentdiff_1_max_a_b), .b(out_12), .out(subtractor_2_out), .bin(undriven));  // open: bout
  Adder #(.width(4)) adder_2 (.a(subtractor_2_out), .b(4'b0000), .out(Output_Exponent), .cin(1'b1));  // open: cout

  assign Output__Fraction = out_9[11:1];
  assign Output_Sign = out_10;
endmodule

module ExponentDiff (
  input  [3:0] A,
  input  [3:0] B,
  output [3:0] abs_A_B,
  output [3:0] Max_A_B
);

  wire subtractor_1_bout;
  wire [3:0] negator_1_out, subtractor_1_out;

  Subtractor #(.width(4)) subtractor_1 (.a(A), .b(B), .out(subtractor_1_out), .bout(subtractor_1_bout));  // open: bin
  Negator #(.width(4)) negator_1 (.in(subtractor_1_out), .out(negator_1_out));
  Multiplexer #(.width(4), .enable("false")) multiplexer_1 (
    .in0(subtractor_1_out), .in1(negator_1_out), .out(abs_A_B), .sel(subtractor_1_bout));
  Multiplexer #(.width(4), .enable("false")) multiplexer_2 (.in0(A), .in1(B), .out(Max_A_B), .sel(subtractor_1_bout));
endmodule

module fraction_sign_set (
  input  [11:0] F,
  input  S,
  output [12:0] F_prime
);

  wire [12:0] bit_extender_1_out, negator_1_out;

  assign bit_extender_1_out = {{1{1'b0}}, F};  // Bit_Extender bit_extender_1
  Negator #(.width(13)) negator_1 (.in(bit_extender_1_out), .out(negator_1_out));
  Multiplexer #(.width(13), .enable("false")) multiplexer_1 (
    .in0(bit_extender_1_out), .in1(negator_1_out), .out(F_prime), .sel(S));
endmodule

module twos_complement_if_negative (
  input  [13:0] in_1,
  output Sign,
  output [12:0] Output
);

  wire [12:0] negator_1_out;

  Negator #(.width(13)) negator_1 (.in(in_1[12:0]), .out(negator_1_out));
  Multiplexer #(.width(13), .enable("false")) multiplexer_1 (
    .in0(in_1[12:0]), .in1(negator_1_out), .out(Output), .sel(in_1[13]));

  assign Sign = in_1[13];
endmodule
