// Logisim project ALU.circ as structural Verilog: 1 circuit, main circuit main
module main (
  input  [7:0] rs,
  input  [7:0] rt,
  input  [2:0] op,
  output [7:0] Operation
);

  wire [7:0] adder_1_out, and_1_out, nor_1_out, or_1_out, subtractor_1_out;

  Adder adder_1 (.a(rt), .b(rs), .out(adder_1_out));  // open: cin, cout
  Subtractor subtractor_1 (.a(rs), .b(rt), .out(subtractor_1_out));  // open: bin, bout
  assign and_1_out = rs & rt;  // AND_Gate and_1, 8 bits wide
  assign or_1_out = rs | rt;  // OR_Gate or_1, 8 bits wide
  assign nor_1_out = ~(rs | rt);  // NOR_Gate nor_1, 8 bits wide
  Multiplexer #(.select(3), .width(8), .enable("false")) multiplexer_1 (
    .in0(adder_1_out), .in1(subtractor_1_out), .in2(and_1_out), .in3(or_1_out), .in4(nor_1_out),
    .out(Operation), .sel(op));  // open: in5, in6, in7
endmodule
