// Logisim project MIPS.circ as structural Verilog: 5 circuits, main circuit main
module main (
  output [7:0] out_1,
  output [7:0] zero,
  output [7:0] t0,
  output [7:0] t1,
  output [7:0] t2,
  output [7:0] t3,
  output [7:0] t4,
  output [7:0] sp
);

  wire clock_1_out, control_extractor_1_destination_selector, control_extractor_1_immediate_got2_selector,
       control_extractor_1_memory_enable, control_extractor_1_r_enable,
       control_extractor_1_write_value_selector;
  wire [1:0] PC_MUX_Select_pc_mux_select;
  wire [2:0] control_extractor_1_function;
  wire [3:0] extractor_1_dst_reg, extractor_1_dst_reg2__for_i, extractor_1_opcode, extractor_1_shft_amnt,
       extractor_1_src_reg1, extractor_1_src_reg2, multiplexer_2_out;
  wire [7:0] adder_1_out, adder_2_out, bit_extender_1_out, extractor_1_immediate,
       extractor_1_target_jump_address, main_1_p2, main_1_p3, main_1_p4, multiplexer_1_out,
       multiplexer_3_out, ram_1_data, reg_file_1_datagot2;
  wire [11:0] rom_2_data;
  wire [19:0] rom_1_data;

  Register #(.trigger("falling")) register_1 (
    .D(multiplexer_1_out), .en(1'b1), .Q(out_1), .clk(clock_1_out));  // open: clr
  Adder adder_1 (.a(8'h1), .b(out_1), .out(adder_1_out));  // open: cin, cout
  Multiplexer #(.select(2), .width(8), .enable("false")) multiplexer_1 (
    .in0(adder_1_out), .in1(extractor_1_immediate), .in2(extractor_1_target_jump_address),
    .out(multiplexer_1_out), .sel(PC_MUX_Select_pc_mux_select));  // open: in3
  ROM #(.dataWidth(20)) rom_1 (.addr(out_1), .data(rom_1_data));  // open: sel
  PC_MUX_Selector PC_MUX_Select (
    .Datagot1(reg_file_1_datagot2), .Datagot2(main_1_p3), .Opcode(extractor_1_opcode),
    .PC_MUX_Select(PC_MUX_Select_pc_mux_select));
  Extractor extractor_1 (
    .Instruction(rom_1_data), .Shft_Amnt(extractor_1_shft_amnt), .Dst_Reg(extractor_1_dst_reg),
    .Src_Reg2(extractor_1_src_reg2), .Src_Reg1(extractor_1_src_reg1), .Opcode(extractor_1_opcode),
    .Immediate(extractor_1_immediate), .dst_reg2__for_I(extractor_1_dst_reg2__for_i),
    .Target_Jump_Address(extractor_1_target_jump_address));
  Clock clock_1 (.out(clock_1_out));
  assign bit_extender_1_out = {{4{1'b0}}, extractor_1_opcode};  // Bit_Extender bit_extender_1
  Multiplexer #(.width(4), .enable("false")) multiplexer_2 (
    .in0(extractor_1_dst_reg), .in1(extractor_1_dst_reg2__for_i), .out(multiplexer_2_out),
    .sel(control_extractor_1_destination_selector));
  ROM #(.dataWidth(12)) rom_2 (.addr(bit_extender_1_out), .data(rom_2_data), .sel(1'b1));
  Control_Extractor control_extractor_1 (
    .Control(rom_2_data), .Write_Value_Selector(control_extractor_1_write_value_selector),
    .Destination_selector(control_extractor_1_destination_selector),
    .Memory_Enable(control_extractor_1_memory_enable),
    .Immediate_Got2_selector(control_extractor_1_immediate_got2_selector),
    .R_Enable(control_extractor_1_r_enable), .\function (control_extractor_1_function));
  // ALU_main main_1: pin names not known; wires that end beside it: control_extractor_1_function, main_1_p2, main_1_p3, main_1_p4, extractor_1_shft_amnt
  Reg_File reg_file_1 (
    .Value(multiplexer_3_out), .ReadWhich1(extractor_1_src_reg1), .Enable(control_extractor_1_r_enable),
    .WriteRegister(multiplexer_2_out), .ReadWhich2(extractor_1_src_reg2), .CLK(clock_1_out),
    .DataGot1(main_1_p3), .DataGot2(reg_file_1_datagot2), .zero(zero), .t0(t0), .t1(t1), .t2(t2), .t3(t3),
    .t4(t4), .sp(sp));
  Multiplexer #(.width(8), .enable("false")) multiplexer_3 (
    .in0(main_1_p2), .in1(ram_1_data), .out(multiplexer_3_out), .sel(control_extractor_1_write_value_selector));
  Multiplexer #(.width(8), .enable("false")) multiplexer_4 (
    .in0(reg_file_1_datagot2), .in1(extractor_1_immediate), .out(main_1_p4),
    .sel(control_extractor_1_immediate_got2_selector));
  Adder adder_2 (.a(main_1_p3), .b(extractor_1_immediate), .out(adder_2_out));  // open: cin, cout
  RAM #(.bus("separate")) ram_1 (
    .addr(adder_2_out), .data(ram_1_data), .str(control_extractor_1_memory_enable), .sel(1'b1),
    .clk(clock_1_out), .ld(1'b1), .clr(1'b0));  // open: din

  // Notes on the sheet:
  //   contents of rom_1 (hex, n*v repeats v):
  //   d3720 d2240 e2020 d4740 b4250 15031 a3011 3150 c3540 84205 343ff 43103 60100 d2240 e2020 d4740 b4250
  //   15031 a3011 3150 c3540 84205 343ff
  //   contents of rom_2 (hex, n*v repeats v):
  //   900 b00 40 7a0 5a0 3a0 0 0 1a0 130 d00 700 500 100 300 25*0 11 100 0 0 10 100 22*0 1 100
endmodule

module Reg_File (
  input  [7:0] Value,
  input  [3:0] ReadWhich1,
  input  Enable,
  input  [3:0] WriteRegister,
  input  [3:0] ReadWhich2,
  input  CLK,
  output [7:0] DataGot1,
  output [7:0] DataGot2,
  output [7:0] zero,
  output [7:0] t0,
  output [7:0] t1,
  output [7:0] t2,
  output [7:0] t3,
  output [7:0] t4,
  output [7:0] sp
);

  wire decoder_1_out0, decoder_1_out1, decoder_1_out2, decoder_1_out3, decoder_1_out4, decoder_1_out5,
       decoder_1_out6;

  Decoder #(.select(4)) decoder_1 (
    .out0(decoder_1_out0), .out1(decoder_1_out1), .out2(decoder_1_out2), .out3(decoder_1_out3),
    .out4(decoder_1_out4), .out5(decoder_1_out5), .out6(decoder_1_out6), .sel(WriteRegister), .en(Enable));  // open: out7, out8, out9, out10, out11, out12, out13, out14, out15
  Register #(.trigger("falling")) u_zero (.D({8{1'b0}}), .en(decoder_1_out0), .Q(zero));  // open: clk, clr
  Register #(.trigger("falling")) u_t0 (.D(Value), .en(decoder_1_out1), .Q(t0), .clk(CLK));  // open: clr
  Register #(.trigger("falling")) u_t1 (.D(Value), .en(decoder_1_out2), .Q(t1), .clk(CLK));  // open: clr
  Register #(.trigger("falling")) u_t2 (.D(Value), .en(decoder_1_out3), .Q(t2), .clk(CLK));  // open: clr
  Register #(.trigger("falling")) u_t3 (.D(Value), .en(decoder_1_out4), .Q(t3), .clk(CLK));  // open: clr
  Register #(.trigger("falling")) u_t4 (.D(Value), .en(decoder_1_out5), .Q(t4), .clk(CLK));  // open: clr
  Register #(.trigger("falling")) u_sp (.D(Value), .en(decoder_1_out6), .Q(sp), .clk(CLK));  // open: clr
  Multiplexer #(.select(4), .width(8)) multiplexer_1 (
    .in0(zero), .in1(t0), .in2(t1), .in3(t2), .in4(t3), .in5(t4), .in6(sp), .in7(8'h1), .out(DataGot1),
    .sel(ReadWhich1), .en(1'b1));  // open: in8, in9, in10, in11, in12, in13, in14, in15
  Multiplexer #(.select(4), .width(8)) multiplexer_2 (
    .in0(zero), .in1(t0), .in2(t1), .in3(t2), .in4(t3), .in5(t4), .in6(sp), .in7(8'h1), .out(DataGot2),
    .sel(ReadWhich2), .en(1'b1));  // open: in8, in9, in10, in11, in12, in13, in14, in15
endmodule

module Extractor (
  input  [19:0] Instruction,
  output [3:0] Shft_Amnt,
  output [3:0] Dst_Reg,
  output [3:0] Src_Reg2,
  output [3:0] Src_Reg1,
  output [3:0] Opcode,
  output [7:0] Immediate,
  output [3:0] dst_reg2__for_I,
  output [7:0] Target_Jump_Address
);


  assign Dst_Reg = Instruction[7:4];
  assign dst_reg2__for_I = Instruction[11:8];
  assign Immediate = Instruction[7:0];
  assign Opcode = Instruction[19:16];
  assign Shft_Amnt = Instruction[3:0];
  assign Src_Reg1 = Instruction[15:12];
  assign Src_Reg2 = Instruction[11:8];
  assign Target_Jump_Address = Instruction[15:8];
endmodule

module PC_MUX_Selector (
  input  [7:0] Datagot1,
  input  [7:0] Datagot2,
  input  [3:0] Opcode,
  output [1:0] PC_MUX_Select
);

  wire comparator_1_gt, comparator_1_lt;
  wire [0:0] comparator_1_eq, Is_not_equal_out;

  Comparator comparator_1 (
    .a(Datagot1), .b(Datagot2), .gt(comparator_1_gt), .eq(comparator_1_eq[0]), .lt(comparator_1_lt));
  or Is_not_equal (Is_not_equal_out[0], comparator_1_gt, comparator_1_lt);
  Multiplexer #(.select(4), .width(2), .enable("false")) multiplexer_1 (
    .in0(2'b00), .in1(2'b00), .in2(2'b00), .in3(2'b00), .in4(2'b00), .in5(2'b00), .in6(2'b10),
    .in7({1'b0, comparator_1_eq[0]}), .in8(2'b00), .in9(2'b00), .in10(2'b00), .in11(2'b00), .in12(2'b00),
    .in13(2'b00), .in14(2'b00), .in15({1'b0, Is_not_equal_out[0]}), .out(PC_MUX_Select), .sel(Opcode));
endmodule

module Control_Extractor (
  input  [11:0] Control,
  output Write_Value_Selector,
  output Destination_selector,
  output Memory_Enable,
  output Immediate_Got2_selector,
  output R_Enable,
  output [2:0] \function 
);


  assign Destination_selector = Control[5];
  assign \function  = Control[11:9];
  assign Immediate_Got2_selector = Control[7];
  assign Memory_Enable = Control[6];
  assign R_Enable = Control[8];
  assign Write_Value_Selector = Control[4];
endmodule
